# Fritzing sketch led_bar (saved by Fritzing 1.0.5)
breadboards: 1

parts:
  D1 = LED_BARGRAPH_10 [package=led_bargaph_10]
  IC1 = SHIFT REGISTER [package=dil16]
  R1 = Resistor [tolerance=±5% resistance=330 package="1206 [SMD]"]
  R2 = Resistor [tolerance=±5% resistance=330 package="1206 [SMD]"]
  R3 = Resistor [tolerance=±5% resistance=330 package="1206 [SMD]"]
  R4 = Resistor [tolerance=±5% resistance=330 package="1206 [SMD]"]
  R5 = Resistor [tolerance=±5% resistance=330 package="1206 [SMD]"]
  R6 = Resistor [tolerance=±5% resistance=330 package="1206 [SMD]"]
  R7 = Resistor [tolerance=±5% resistance=330 package="1206 [SMD]"]
  R8 = Resistor [tolerance=±5% resistance=330 package="1206 [SMD]"]
  R9 = Resistor [tolerance=±5% resistance=330 package="1206 [SMD]"]
  R10 = Resistor [tolerance=±5% resistance=330 package="1206 [SMD]"]
  IC2 = SHIFT REGISTER [package=dil16]
  A1 = Teensy 4.0

nets:
  GND: D1.A_A, D1.B_A, D1.C_A, D1.D_A, D1.E_A, D1.F_A, D1.G_A, D1.H_A, D1.I_A, D1.J_A, IC1.GND, IC2.GND, A1.pin_1, A1.pin_17
  N1: D1.J_C, R1.Pin_0
  N2: D1.I_C, R2.Pin_0
  N3: D1.H_C, R3.Pin_0
  N4: D1.G_C, R4.Pin_0
  N5: D1.F_C, R5.Pin_0
  N6: D1.E_C, R6.Pin_0
  N7: D1.D_C, R7.Pin_0
  N8: D1.C_C, R8.Pin_0
  N9: D1.B_C, R9.Pin_0
  N10: D1.A_C, R10.Pin_0
  N11: IC1.QB, R9.Pin_1
  N12: IC1.QC, R8.Pin_1
  N13: IC1.QD, R7.Pin_1
  N14: IC1.QE, R6.Pin_1
  N15: IC1.QF, R5.Pin_1
  N16: IC1.QG, R4.Pin_1
  N17: IC1.QH, R3.Pin_1
  N18: IC1.QH*, IC2.SER
  N19: IC1.SCK, IC2.SCK, A1.pin_6
  N20: IC1.RCK, IC2.RCK, A1.pin_7
  N21: IC1.SER, A1.pin_5
  N22: IC1.QA, R10.Pin_1
  VCC: IC1.VCC, IC2.VCC, A1.pin33
  N23: R1.Pin_1, IC2.QB
  N24: R2.Pin_1, IC2.QA

custom parts:
  Teensy 4.0: The Teensy is a complete USB-based microcontoller development system, in a very small footprint, capable of implementing many types of projects. All programming is done via the USB port. No special programmer is needed, only a standard micro-USB cable and a PC or Macintosh with a USB port. (Oct 2023 added the VBUS pad at user request.)
